# Fritzing sketch schematic (saved by Fritzing 0.9.2b)
breadboards: 1

parts:
  RHT1 = Humidity and Temperature Sensor RHT03
  Part1 = Arduino Uno (Rev3)
  R1 = Resistor [tolerance=±5% resistance=10k package=THT]
  C1 = Ceramic Capacitor [capacitance=100nF package="100 mil [THT, multilayer]"]
  LCD1 = LCD screen
  U1 = BMP085 Pressure Sensor [package=bmp085]  # not connected
  Part2 = Barometric Pressure Sensor - BMP085 Breakout

nets:
  VCC: RHT1.Vcc, Part1.5V, R1.Pin_1, C1.1, LCD1.LED+
  N1: RHT1.Data-signal, Part1.D4, R1.Pin_0
  GND: RHT1.GND_2, Part1.GND, C1.0, LCD1.LED-, Part2.GND
  N2: Part1.A4/SDA, LCD1.DB6, Part2.SDA
  N3: Part1.A5/SCL, LCD1.DB7, Part2.SCL
  3V3: Part1.3V3, Part2.VCC

notes:
  Vcc
  GND

custom parts:
  Barometric Pressure Sensor - BMP085 Breakout: Description: This is a simple breakout board for the BMP085 high-precision, low-power barometric pressure sensor. The BMP085 offers a measuring range of 300 to 1100 hPa with an absolute accuracy of down to 0.03 hPa. It's based on piezo-resistive technology for EMC robustness, high accuracy and linearity as well as long term stability. This sensor supports a voltage supply between 1.8 and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
